// Logisim project 5 bit d flip flop counter.circ as structural Verilog: 1 circuit, main circuit main
module main (
  output out_1,
  output out_2,
  output out_3,
  output out_4,
  output out_5
);

  wire clock_1_out, d_ff_1_q, d_ff_2_q, d_ff_3_q, d_ff_4_q, d_ff_5_q;

  Clock clock_1 (.out(clock_1_out));
  D_Flip_Flop d_ff_1 (.clk(clock_1_out), .D(out_1), .Q(d_ff_1_q));  // open: Qn, preset, en, reset
  D_Flip_Flop d_ff_2 (.clk(d_ff_1_q), .D(out_2), .Q(d_ff_2_q));  // open: Qn, preset, en, reset
  D_Flip_Flop d_ff_3 (.clk(d_ff_2_q), .D(out_3), .Q(d_ff_3_q));  // open: Qn, preset, en, reset
  D_Flip_Flop d_ff_4 (.clk(d_ff_3_q), .D(out_4), .Q(d_ff_4_q));  // open: Qn, preset, en, reset
  D_Flip_Flop d_ff_5 (.clk(d_ff_4_q), .D(out_5), .Q(d_ff_5_q));  // open: Qn, preset, en, reset
  not not_1 (out_1, d_ff_1_q);
  not not_2 (out_2, d_ff_2_q);
  not not_3 (out_3, d_ff_3_q);
  not not_4 (out_4, d_ff_4_q);
  not not_5 (out_5, d_ff_5_q);
endmodule
