// Logisim project nand memory.circ as structural Verilog: 1 circuit, main circuit main
module main (
  input  a,
  input  b,
  output out_1,
  output out_2
);

  nand nand_1 (out_1, a, out_2);
  nand nand_2 (out_2, out_1, b);
endmodule
