// Logisim project one of four and one of eight decoders.circ as structural Verilog: 1 circuit, main circuit main
module main (
  input  E,
  input  E_2,
  input  S0,
  input  S0_2,
  input  S1,
  input  in_6,
  input  in_7,
  output _1_of_4_decoder,
  output _1_of_8_decoder,
  output out_10,
  output out_11,
  output out_12,
  output out_13,
  output Y0,
  output out_15,
  output out_16,
  output Y1,
  output Y1_2,
  output Y2,
  output Y2_2,
  output Y3,
  output Y3_2,
  output Y4,
  output Y5,
  output Y6,
  output Y7
);

  not not_1 (_1_of_4_decoder, E);
  not not_2 (out_10, S0);
  not not_3 (out_12, S1);
  and and_1 (Y0, E, out_10, out_12);
  and and_2 (Y1, E, out_12, S0);
  and and_3 (Y2, E, out_10, S1);
  and and_4 (Y3, E, S0, S1);
  not not_4 (_1_of_8_decoder, E_2);
  not not_5 (out_11, S0_2);
  not not_6 (out_13, in_6);
  not not_7 (out_15, in_7);
  and and_5 (out_16, E_2, out_11, out_13, out_15);
  and and_6 (Y1_2, E_2, out_11, out_13, in_7);
  and and_7 (Y2_2, E_2, out_11, in_6, out_15);
  and and_8 (Y3_2, E_2, out_11, in_6, in_7);
  and and_9 (Y4, E_2, S0_2, out_13, out_15);
  and and_10 (Y5, E_2, S0_2, out_13, in_7);
  and and_11 (Y6, E_2, S0_2, in_6, out_15);
  and and_12 (Y7, E_2, S0_2, in_6, in_7);

  // Notes on the sheet:
  //   S1
  //   S2
  //   Y0
endmodule
