// Logisim project ripple carry.circ as structural Verilog: 1 circuit, main circuit main
module main (
  input  A0,
  input  B0,
  input  A1,
  input  B1,
  input  A2,
  input  B2,
  output S0,
  output S1,
  output Cout,
  output S2,
  output Cout_2
);

  wire and_1_out, and_2_out, and_3_out, and_4_out, and_5_out, and_6_out, or_1_out, xor_1_out, xor_3_out,
       xor_5_out;

  xor xor_1 (xor_1_out, A0, B0);
  and and_1 (and_1_out, 1'b0, xor_1_out);
  and and_2 (and_2_out, A0, B0);
  xor xor_2 (S0, xor_1_out, 1'b0);
  or or_1 (or_1_out, and_1_out, and_2_out);
  xor xor_3 (xor_3_out, A1, B1);
  xor xor_4 (S1, xor_3_out, or_1_out);
  and and_3 (and_3_out, or_1_out, xor_3_out);
  and and_4 (and_4_out, A1, B1);
  xor xor_5 (xor_5_out, A2, B2);
  or or_2 (Cout, and_3_out, and_4_out);
  xor xor_6 (S2, xor_5_out, Cout);
  and and_5 (and_5_out, Cout, xor_5_out);
  and and_6 (and_6_out, A2, B2);
  or or_3 (Cout_2, and_5_out, and_6_out);

  // Notes on the sheet:
  //   Cin
  //   Cout
endmodule
