// Logisim project sr and d type latches.circ as structural Verilog: 1 circuit, main circuit main
module main (
  input  in_1,
  input  in_2,
  input  in_3,
  input  in_4,
  output out_5,
  output out_6,
  output out_7,
  output out_8
);

  wire nand_1_out, nand_2_out;

  nor nor_1 (out_5, in_1, out_6);
  nor nor_2 (out_6, out_5, in_2);
  nand nand_1 (nand_1_out, in_3, in_4);
  nand nand_2 (nand_2_out, nand_1_out, in_4);
  nand nand_3 (out_7, nand_1_out, out_8);
  nand nand_4 (out_8, out_7, nand_2_out);

  // Notes on the sheet:
  //   SR Latch
  //   D-type Latch
endmodule
